// Logisim project somador_subtrator.circ as structural Verilog: 4 circuits, main circuit main
module main (
  input  [6:0] A,
  input  [6:0] B,
  input  in_3,
  input  _0____Soma,
  input  in_5
);

  wire A0C2, A1C2, A2C2, A3C2, A4C2, A5C2, A6C2, B0C2, B1C2, B2C2, B3C2, B4C2, B5C2, B6C2, not_1_out,
       not_2_out, not_3_out, not_4_out, not_5_out, not_6_out, S0, S1, S2, S3, S4, S5, S6, Ts0, Ts1, Ts2, Ts3,
       Ts4, Ts5, Ts6, xor_1_out;
  wire [2:0] HexS1;
  wire [3:0] HexS0;

  _7_Segment_Display u_7_segment_display_1 (.g(1'b1), .b(in_3), .c(in_3));  // open: f, a, e, d, dp
  _7_Segment_Display u_7_segment_display_2 (.g(1'b1), .f(in_3), .e(in_3));  // open: a, b, d, c, dp
  Hex_Digit_Display hex_digit_display_1 (.value({1'b0, A[6:4]}));  // open: dp
  Hex_Digit_Display hex_digit_display_2 (.value(A[3:0]));  // open: dp
  not not_1 (not_1_out, _0____Soma);
  _7_Segment_Display u_7_segment_display_3 (.g(1'b1), .b(not_1_out), .c(not_3_out));  // open: f, a, e, d, dp
  not not_2 (not_2_out, _0____Soma);
  _7_Segment_Display u_7_segment_display_4 (.g(1'b1), .f(not_2_out), .e(not_3_out));  // open: a, b, d, c, dp
  not not_3 (not_3_out, _0____Soma);
  _7_Segment_Display u_7_segment_display_5 (.g(1'b1), .b(in_5), .c(in_5));  // open: f, a, e, d, dp
  _7_Segment_Display u_7_segment_display_6 (.g(1'b1), .f(in_5), .e(in_5));  // open: a, b, d, c, dp
  Hex_Digit_Display hex_digit_display_3 (.value({1'b0, B[6:4]}));  // open: dp
  xor xor_1 (xor_1_out, Ts6, Ts5);
  LED Overflow (.in(xor_1_out));
  Hex_Digit_Display hex_digit_display_4 (.value(B[3:0]));  // open: dp
  _7_Segment_Display u_7_segment_display_7 (.g(1'b1), .b(not_4_out), .c(not_5_out));  // open: f, a, e, d, dp
  not not_4 (not_4_out, S6);
  _7_Segment_Display u_7_segment_display_8 (.g(1'b1), .f(not_4_out), .e(not_5_out));  // open: a, b, d, c, dp
  Hex_Digit_Display hex_digit_display_5 (.value({1'b0, HexS1}));  // open: dp
  not not_5 (not_5_out, S6);
  Hex_Digit_Display hex_digit_display_6 (.value(HexS0));  // open: dp
  somador_subtrator_completo somador_subtrator_completo_1 (
    .Operacao(_0____Soma), .BitA(A0C2), .BitB(B0C2), .Te(1'b0), .S(S0), .Ts(Ts0));
  complemento_de_2 complemento_de_2_1 (
    .Sinal_Numero(in_3), .Bit0(A[0]), .Bit1(A[1]), .Bit2(A[2]), .Bit3(A[3]), .Bit4(A[4]), .Bit5(A[5]),
    .Bit6(A[6]), .out_9({A6C2, A5C2, A4C2, A3C2, A2C2, A1C2, A0C2}));
  somador_subtrator_completo somador_subtrator_completo_2 (
    .Operacao(_0____Soma), .BitA(A4C2), .BitB(B4C2), .Te(Ts3), .S(S4), .Ts(Ts4));
  somador_subtrator_completo somador_subtrator_completo_3 (
    .Operacao(_0____Soma), .BitA(A1C2), .BitB(B1C2), .Te(Ts0), .S(S1), .Ts(Ts1));
  complemento_de_2 complemento_de_2_2 (
    .Sinal_Numero(in_5), .Bit0(B[0]), .Bit1(B[1]), .Bit2(B[2]), .Bit3(B[3]), .Bit4(B[4]), .Bit5(B[5]),
    .Bit6(B[6]), .out_9({B6C2, B5C2, B4C2, B3C2, B2C2, B1C2, B0C2}));
  somador_subtrator_completo somador_subtrator_completo_4 (
    .Operacao(_0____Soma), .BitA(A5C2), .BitB(B5C2), .Te(Ts4), .S(S5), .Ts(Ts5));
  somador_subtrator_completo somador_subtrator_completo_5 (
    .Operacao(_0____Soma), .BitA(A2C2), .BitB(B2C2), .Te(Ts1), .S(S2), .Ts(Ts2));
  not not_6 (not_6_out, S6);
  somador_subtrator_completo somador_subtrator_completo_6 (
    .Operacao(_0____Soma), .BitA(A6C2), .BitB(B6C2), .Te(Ts5), .S(S6), .Ts(Ts6));
  complemento_de_2 complemento_de_2_3 (
    .Sinal_Numero(not_6_out), .Bit0(S0), .Bit1(S1), .Bit2(S2), .Bit3(S3), .Bit4(S4), .Bit5(S5), .Bit6(S6),
    .out_9({HexS1, HexS0}));
  somador_subtrator_completo somador_subtrator_completo_7 (
    .Operacao(_0____Soma), .BitA(A3C2), .BitB(B3C2), .Te(Ts2), .S(S3), .Ts(Ts3));

  // Other names for the same wires on the sheet: S0C2 = HexS0[0]; S1C2 = HexS0[1]; S2C2 = HexS0[2]; S3C2 = HexS0[3];
  //   S4C2 = HexS1[0]; S5C2 = HexS1[1]; S6C2 = HexS1[2]; HexA0[3:0] = A[3:0]; HexA1[2:0] = A[6:4];
  //   HexB0[3:0] = B[3:0]; HexB1[2:0] = B[6:4]; M = _0____Soma; SNA = in_3; SNB = in_5

  // Notes on the sheet:
  //   0 -> Negativo (com C2)
  //   1 -> Positivo (sem C2)
  //   1 -> Subtração
  //   0 -> Negativo (com C2)
  //   1 -> Positivo (sem C2)
  //   =
endmodule

module somador_subtrator_completo (
  input  Operacao,
  input  BitA,
  input  BitB,
  input  Te,
  output S,
  output Ts
);

  wire and_1_out, and_2_out, and_3_out, and_4_out, and_5_out, and_6_out, and_7_out, and_8_out, and_9_out,
       not_1_out, not_2_out, not_3_out, not_4_out;

  not not_1 (not_1_out, Operacao);
  not not_2 (not_2_out, BitA);
  not not_3 (not_3_out, BitB);
  not not_4 (not_4_out, Te);
  and and_1 (and_1_out, not_2_out, not_3_out, Te);
  and and_2 (and_2_out, not_2_out, BitB, not_4_out);
  and and_3 (and_3_out, BitA, not_3_out, not_4_out);
  and and_4 (and_4_out, BitA, BitB, Te);
  and and_5 (and_5_out, BitB, Te);
  and and_6 (and_6_out, not_1_out, BitA, Te);
  and and_7 (and_7_out, not_1_out, BitA, BitB);
  and and_8 (and_8_out, Operacao, not_2_out, Te);
  and and_9 (and_9_out, Operacao, not_2_out, BitB);
  or or_1 (S, and_1_out, and_2_out, and_3_out, and_4_out);
  or or_2 (Ts, and_5_out, and_6_out, and_7_out, and_8_out, and_9_out);

  // Notes on the sheet:
  //   Chave da Operação
  //   0 -> Soma
  //   1 -> Subtração
endmodule

module meio_somador (
  input  BitA,
  input  BitB,
  output S,
  output Ts
);

  xor xor_1 (S, BitB, BitA);
  and and_1 (Ts, BitB, BitA);
endmodule

module complemento_de_2 (
  input  Sinal_Numero,
  input  Bit0,
  input  Bit1,
  input  Bit2,
  input  Bit3,
  input  Bit4,
  input  Bit5,
  input  Bit6,
  output [6:0] out_9
);

  wire BitF0, BitF1, BitF2, BitF3, BitF4, BitF5, BitF6, not_1_out, not_2_out, not_3_out, not_4_out,
       not_5_out, not_6_out, not_7_out, Soma_C2, Ts0C2, Ts1C2, Ts2C2, Ts3C2, Ts4C2, Ts5C2, Ts6C2;

  not not_1 (not_1_out, Bit0);
  not not_2 (not_2_out, Bit1);
  not not_3 (not_3_out, Bit2);
  not not_4 (not_4_out, Bit3);
  not not_5 (not_5_out, Bit4);
  not not_6 (not_6_out, Bit5);
  not not_7 (not_7_out, Bit6);
  not not_8 (Soma_C2, Sinal_Numero);
  xor xor_1 (BitF0, Sinal_Numero, not_1_out);
  xor xor_2 (BitF1, Sinal_Numero, not_2_out);
  xor xor_3 (BitF2, Sinal_Numero, not_3_out);
  xor xor_4 (BitF3, Sinal_Numero, not_4_out);
  xor xor_5 (BitF4, Sinal_Numero, not_5_out);
  xor xor_6 (BitF5, Sinal_Numero, not_6_out);
  xor xor_7 (BitF6, Sinal_Numero, not_7_out);
  meio_somador meio_somador_1 (.BitA(BitF0), .BitB(Soma_C2), .S(out_9[0]), .Ts(Ts0C2));
  meio_somador meio_somador_2 (.BitA(BitF1), .BitB(Ts0C2), .S(out_9[1]), .Ts(Ts1C2));
  meio_somador meio_somador_3 (.BitA(BitF2), .BitB(Ts1C2), .S(out_9[2]), .Ts(Ts2C2));
  meio_somador meio_somador_4 (.BitA(BitF3), .BitB(Ts2C2), .S(out_9[3]), .Ts(Ts3C2));
  meio_somador meio_somador_5 (.BitA(BitF4), .BitB(Ts3C2), .S(out_9[4]), .Ts(Ts4C2));
  meio_somador meio_somador_6 (.BitA(BitF5), .BitB(Ts4C2), .S(out_9[5]), .Ts(Ts5C2));
  meio_somador meio_somador_7 (.BitA(BitF6), .BitB(Ts5C2), .S(out_9[6]), .Ts(Ts6C2));

  // Other names for the same wires on the sheet: Bit0C2 = out_9[0]; Bit1C2 = out_9[1]; Bit2C2 = out_9[2];
  //   Bit3C2 = out_9[3]; Bit4C2 = out_9[4]; Bit5C2 = out_9[5]; Bit6C2 = out_9[6]

  // Notes on the sheet:
  //   Sinal_Numero
  //   0 -> Negativo (com C2)
  //   1 -> Positivo (sem C2)
  //   C2
endmodule
